// Digital circuit Homework2_Counter.dig as structural Verilog
module Homework2_Counter (
  input  direction,
  input  clk,
  output Q1,
  output Q0
);

  wire not_1_out, xnor_1_out, xor_1_out;

  xnor xnor_1 (xnor_1_out, Q0, direction);
  not not_1 (not_1_out, Q0);
  xor xor_1 (xor_1_out, xnor_1_out, Q1);
  D_FF d_ff_1 (.D(xor_1_out), .C(clk), .Q(Q1));  // open: nQ
  D_FF d_ff_2 (.D(not_1_out), .C(clk), .Q(Q0));  // open: nQ
endmodule
