// Digital circuit Homework2_Question7.dig as structural Verilog
module Homework2_Question7 (
  input  I,
  input  clk,
  output X,
  output S1,
  output S0
);

  wire and_1_out, and_2_out, not_1_out;

  not not_1 (not_1_out, S1);
  and and_1 (and_1_out, not_1_out, S0);
  and and_2 (and_2_out, S1, S0, I);
  or or_1 (X, not_1_out, S0);
  D_FF d_ff_1 (.D(and_1_out), .C(clk), .Q(S1));  // open: nQ
  D_FF d_ff_2 (.D(and_2_out), .C(clk), .Q(S0));  // open: nQ
endmodule
